# Fritzing sketch Flaschenfueller1 (saved by Fritzing 0.9.3b)

parts:
  Bauteil2 = Arduino Uno (Rev3) - ICSP
  Bauteil3 = LCD Keypad Shield  # not connected
  Bauteil4 = Adafruit Proto Shield for Arduino Kit - v.5
  Q1 = NPN-Transistor [package="TO92 [THT]"]
  R1 = Trimmer Potentiometer [maximum_resistance=300kΩ knob_status=50% power=0.5W package=THT]
  U1 = Module 4 Relais 5V [package="Module 4 Relais 5V"]
  JACK1 = 2.1mm Barrel Jack with Terminal Block

nets:
  N1: Bauteil2.A0, Bauteil4.A5
  N2: Bauteil2.A1, Bauteil4.A4, Bauteil4.1#183, Bauteil4.P$5#184, Q1.C
  N3: Bauteil2.ICSP_MOSI, Bauteil2.D11_PWM/MOSI, U1.IN3
  N4: Bauteil2.D12/MISO, U1.IN2
  N5: Bauteil2.D13/SCK, U1.IN1
  GND: Bauteil2.GND, Bauteil4.P$11#14, Bauteil4.GND, Bauteil4.1#156, Bauteil4.P$5#157, Bauteil4.P$6#158, Bauteil4.N$108, Q1.E, R1.wiper
  5V: Bauteil2.5V, Bauteil4.+5V, Bauteil4.P$11#237, U1.VCC
  N6: Bauteil4.1#163, Bauteil4.P$5#164, Bauteil4.P$6#165, Bauteil4.N$195, Q1.B, R1.leg2
  N7: Bauteil4.N$81, R1.leg1
  N8: U1.GND, JACK1.NEG
  N9: U1.JD-VCC, JACK1.POS

custom parts:
  LCD Keypad Shield: It consists of a 1602 white character blue backlight LCD. The keypad consists of 5 keys — select, up, right, down and left. To save the digital IO pins, the keypad interface uses only one ADC channel. The key value is read through a 5 stage voltage divider.
  Adafruit Proto Shield for Arduino Kit - v.5: Arduino prototyping shield designed by Adafruit Industries
  Module 4 Relais 5V: Module 4 Relais 5V 4x SPD-06VDC-SD-C
